// Logisim project Multi.circ as structural Verilog: 3 circuits, main circuit Robot
module Robot (
  input  reset,
  input  enable,
  input  clock,
  input  B0,
  input  END,
  input  LAUNCH,
  output INIT,
  output CLEAR_C,
  output ADD,
  output SHR,
  output OK
);

  wire and_1_out, and_2_out, and_3_out, and_4_out, and_5_out, and_6_out, not_1_out, not_2_out, not_3_out,
       not_4_out, Q0_in, Q1, Q1_in, Q2_in, Q3_in, Q4_in;

  not not_1 (not_1_out, LAUNCH);
  not not_2 (not_2_out, LAUNCH);
  not not_3 (not_3_out, B0);
  not not_4 (not_4_out, END);
  and and_1 (and_1_out, not_1_out, OK);
  and and_2 (and_2_out, not_2_out, INIT);
  and and_3 (and_3_out, LAUNCH, INIT);
  and and_4 (and_4_out, not_3_out, not_4_out, Q1);
  and and_5 (and_5_out, END, Q1);
  and and_6 (and_6_out, LAUNCH, OK);
  or or_1 (Q0_in, and_1_out, and_2_out);
  or or_2 (Q1_in, and_3_out, SHR);
  and and_7 (Q2_in, B0, Q1);
  or or_3 (Q3_in, ADD, and_4_out);
  or or_4 (Q4_in, and_5_out, and_6_out);
  D_Flip_Flop Q0 (.clk(clock), .D(Q0_in), .Q(INIT), .preset(reset), .en(enable));  // open: Qn, reset
  D_Flip_Flop Q1__Waiting_State (.clk(clock), .D(Q1_in), .Q(Q1), .en(enable), .reset(reset));  // open: Qn, preset
  D_Flip_Flop Q2 (.clk(clock), .D(Q2_in), .Q(ADD), .en(enable), .reset(reset));  // open: Qn, preset
  D_Flip_Flop Q3 (.clk(clock), .D(Q3_in), .Q(SHR), .en(enable), .reset(reset));  // open: Qn, preset
  D_Flip_Flop Q4 (.clk(clock), .D(Q4_in), .Q(OK), .en(enable), .reset(reset));  // open: Qn, preset
  or or_5 (CLEAR_C, INIT, SHR);

  // Other names for the same wires on the sheet: Q0 = INIT; Q2 = ADD; Q3 = SHR; Q4 = OK
endmodule

module Multi (
  input  enable
);

  wire ADD, CLEAR_C, CLOCK, datapath_1_out_8, END, INIT, LAUNCH, RESET, robot_1_ok, SHIFT;
  wire [7:0] datapath_1_out_9;

  Clock clock_1 (.out(CLOCK));
  Button button_1 (.out(LAUNCH));
  Button button_2 (.out(RESET));
  Robot robot_1 (
    .reset(RESET), .enable(enable), .B0(datapath_1_out_8), .END(END), .LAUNCH(LAUNCH), .INIT(INIT),
    .CLEAR_C(CLEAR_C), .ADD(SHIFT), .SHR(ADD), .OK(robot_1_ok), .clock(CLOCK));
  Datapath datapath_1 (
    .in_1(INIT), .in_2(4'b1100), .in_3(CLEAR_C), .in_4(4'b1011), .in_5(ADD), .in_6(SHIFT), .in_7(CLOCK),
    .out_8(datapath_1_out_8), .out_9(datapath_1_out_9), .out_10(END));
  // Probe on robot_1_ok
  // Probe on datapath_1_out_9

  // Notes on the sheet:
  //   B0
  //   Inputs Datapath
  //   Inputs Automate
  //   Outputs Automate
  //   Outputs Datapath
  //   OK
  //   Result
endmodule

module Datapath (
  input  in_1,
  input  [3:0] in_2,
  input  in_3,
  input  [3:0] in_4,
  input  in_5,
  input  in_6,
  input  in_7,
  output out_8,
  output [7:0] out_9,
  output out_10
);

  wire and_1_out, CARRY, not_1_out, not_2_out, register_1_q, shift_register_1_out;
  wire [2:0] counter_1_q;
  wire [3:0] ADD_RES;

  Register #(.width(1)) register_1 (.D(CARRY), .en(in_5), .Q(register_1_q), .clk(in_7), .clr(in_3));
  Counter #(.width(3), .max('h7)) counter_1 (
    .D(3'b001), .Q(counter_1_q), .clk(and_1_out), .clr(in_1));  // open: load, count, carry
  and and_1 (and_1_out, in_6, in_7);
  not not_1 (not_1_out, counter_1_q[0]);
  and and_2 (out_10, not_1_out, not_2_out, counter_1_q[2]);
  not not_2 (not_2_out, counter_1_q[1]);
  Shift_Register #(.length(4)) shift_register_1 (
    .shift(in_6), .in(register_1_q), .clk(in_7), .out(shift_register_1_out), .load(in_5), .clr(in_1),
    .d0(ADD_RES[3]), .q0(out_9[7]), .d1(ADD_RES[2]), .q1(out_9[6]), .d2(ADD_RES[1]), .q2(out_9[5]),
    .d3(ADD_RES[0]), .q3(out_9[4]));
  Shift_Register #(.length(4)) shift_register_2 (
    .shift(in_6), .in(shift_register_1_out), .clk(in_7), .out(out_8), .load(in_1), .d0(in_4[3]),
    .q0(out_9[3]), .d1(in_4[2]), .q1(out_9[2]), .d2(in_4[1]), .q2(out_9[1]), .d3(in_4[0]), .q3(out_9[0]));  // open: clr
  Adder #(.width(4)) adder_1 (.a(in_2), .b(out_9[7:4]), .out(ADD_RES), .cin(1'b0), .cout(CARRY));

  // Other names for the same wires on the sheet: ADD = in_5; B0 = out_8; CLOCK = in_7; CLR_C = in_3; END = out_10;
  //   INIT = in_1; MULTIPLICANDE[3:0] = in_2; MULTIPLIEUR[3:0] = in_4; REG_2[3:0] = out_9[3:0];
  //   REG_1[3:0] = out_9[7:4]; SHR = in_6
endmodule
