// Logisim project TP1-Archi-CH3-4-5.circ as structural Verilog: 6 circuits, main circuit main
module main (
  input  in_1,
  input  in_2,
  input  in_3,
  input  in_4,
  input  in_5,
  input  in_6,
  output out_7
);


  // Notes on the sheet:
  //   inputs
  //   addr
  //   Multiplexeur 4 vers 1 de 4 bits
endmodule

module Demultiplexeur_1_vers_4_de_1_bit (
  input  [1:0] addr,
  input  \input ,
  output out_3,
  output out_4,
  output out_5,
  output out_6
);

  wire not_1_out, not_2_out, not_3_out, not_4_out;

  not not_1 (not_1_out, addr[1]);
  not not_2 (not_2_out, addr[0]);
  not not_3 (not_3_out, addr[1]);
  not not_4 (not_4_out, addr[0]);
  and and_1 (out_3, not_1_out, not_2_out, \input );
  and and_2 (out_4, not_3_out, addr[0], \input );
  and and_3 (out_5, addr[1], not_4_out, \input );
  and and_4 (out_6, addr[1], addr[0], \input );

  // Notes on the sheet:
  //   Demultiplexeur : 1 vers 4 de 1 bit
endmodule

// bit Add
module _1_bit_Adder (
  input  c_in,
  input  input_1,
  input  input_2,
  output s,
  output c_out
);

  wire and_1_out, and_2_out, and_3_out, xor_1_out;

  xor xor_1 (xor_1_out, input_1, input_2);
  and and_1 (and_1_out, c_in, input_1);
  and and_2 (and_2_out, c_in, input_2);
  and and_3 (and_3_out, input_1, input_2);
  xor xor_2 (s, c_in, xor_1_out);
  or or_1 (c_out, and_1_out, and_2_out, and_3_out);
endmodule

// Mul 1-4/1
module Multiplexeur_4_vers_1_de_1_bit (
  input  [1:0] addr,
  input  addr___00,
  input  addr___01,
  input  addr___10,
  input  addr___11,
  output out_6
);

  wire and_1_out, and_2_out, and_3_out, and_4_out, not_1_out, not_2_out, not_3_out, not_4_out;

  not not_1 (not_1_out, addr[0]);
  not not_2 (not_2_out, addr[1]);
  not not_3 (not_3_out, addr[1]);
  not not_4 (not_4_out, addr[0]);
  and and_1 (and_1_out, not_1_out, not_2_out, addr___00);
  and and_2 (and_2_out, addr[0], not_3_out, addr___01);
  and and_3 (and_3_out, not_4_out, addr[1], addr___10);
  and and_4 (and_4_out, addr[0], addr[1], addr___11);
  ExactlyOne xor_1 (.out(out_6), .in0(and_1_out), .in1(and_2_out), .in2(and_3_out), .in3(and_4_out));

  // Notes on the sheet:
  //   1 bits correspond à la taille des mots
endmodule

module Multiplexeur_4_vers_1_de_4_bits (
  input  [1:0] addr,
  input  [3:0] in_2,
  input  [3:0] in_3,
  input  [3:0] in_4,
  input  [3:0] in_5,
  output [3:0] out_6
);

  Multiplexeur_4_vers_1_de_1_bit multiplexeur_4_vers_1_de_1_bit_1 (
    .addr___00(in_2[0]), .addr___01(in_3[0]), .addr___10(in_4[0]), .addr___11(in_5[0]), .out_6(out_6[0]),
    .addr(addr));
  Multiplexeur_4_vers_1_de_1_bit multiplexeur_4_vers_1_de_1_bit_2 (
    .addr___00(in_2[1]), .addr___01(in_3[1]), .addr___10(in_4[1]), .addr___11(in_5[1]), .out_6(out_6[1]),
    .addr(addr));
  Multiplexeur_4_vers_1_de_1_bit multiplexeur_4_vers_1_de_1_bit_3 (
    .addr___00(in_2[2]), .addr___01(in_3[2]), .addr___10(in_4[2]), .addr___11(in_5[2]), .out_6(out_6[2]),
    .addr(addr));
  Multiplexeur_4_vers_1_de_1_bit multiplexeur_4_vers_1_de_1_bit_4 (
    .addr___00(in_2[3]), .addr___01(in_3[3]), .addr___10(in_4[3]), .addr___11(in_5[3]), .out_6(out_6[3]),
    .addr(addr));

  // Other names for the same wires on the sheet: addr_port[1:0] = addr

  // Notes on the sheet:
  //   4 bits correspond à la taille des mots
endmodule

module _4_bits_Adder (
  input  c_in,
  input  [3:0] in_2,
  input  [3:0] in_3,
  output [3:0] s,
  output c_out
);

  wire n1_bit_adder_1_p4, n1_bit_adder_2_p4, n1_bit_adder_3_p4;

  // _1_bit_Adder 1_bit_adder_1: pin names not known; wires that end beside it: in_2[0], in_3[0], c_in, n1_bit_adder_1_p4, n1_bit_adder_1_p4, s[0]
  // _1_bit_Adder 1_bit_adder_2: pin names not known; wires that end beside it: in_2[1], in_3[1], n1_bit_adder_1_p4, n1_bit_adder_2_p4, n1_bit_adder_2_p4, s[1]
  // _1_bit_Adder 1_bit_adder_3: pin names not known; wires that end beside it: in_2[2], in_3[2], n1_bit_adder_2_p4, n1_bit_adder_3_p4, n1_bit_adder_3_p4, s[2]
  // _1_bit_Adder 1_bit_adder_4: pin names not known; wires that end beside it: in_2[3], in_3[3], n1_bit_adder_3_p4, c_out, s[3]
endmodule
