// Logisim project TP2-Archi-Ch6-1.circ as structural Verilog: 1 circuit, main circuit main
module main (
  input  CMD,
  input  Reset,
  output OUT
);

  wire and_1_out, LED_out, not_1_out;

  not not_1 (not_1_out, OUT);
  and and_1 (and_1_out, not_1_out, CMD);
  Register #(.width(1)) register_1 (.D(and_1_out), .en(1'b1), .Q(OUT), .clk(LED_out), .clr(Reset));
  Clock LED (.out(LED_out));
endmodule
