// Logisim project TP3-Archi-CH7-Compteur.circ as structural Verilog: 2 circuits, main circuit main
module main (
  input  in_1
);

  wire and_1_out, and_2_out, and_3_out, and_4_out, and_5_out, button, clock, enable, not_1_out, not_2_out,
       not_3_out, not_4_out, not_5_out, or_1_out, or_2_out, or_3_out, or_4_out, or_5_out, or_6_out, or_7_out,
       q0_out, q1_q, q2_out, q3_out, q4_q, q5_out, reset;
  wire [15:0] adder_1_out, register_1_q;

  Button button_1 (.out(button));
  Clock clock_1 (.out(clock));
  Register #(.width(16)) register_1 (.D(adder_1_out), .en(enable), .Q(register_1_q), .clk(clock), .clr(reset));
  not not_1 (not_1_out, button);
  not not_2 (not_2_out, button);
  and and_1 (and_1_out, not_2_out, q5_out);
  or or_1 (or_1_out, in_1, q0_out);
  Adder #(.width(16)) adder_1 (.a(16'h1), .b(register_1_q), .out(adder_1_out));  // open: cin, cout
  or or_2 (or_2_out, and_1_out, or_1_out);
  or or_3 (or_3_out, q2_out, q3_out);
  and and_2 (and_2_out, button, q0_out);
  D_Flip_Flop q0 (.clk(clock), .D(or_2_out), .Q(q0_out), .reset(q1_q));  // open: Qn, preset, en
  not not_3 (not_3_out, button);
  and and_3 (and_3_out, not_3_out, q3_out);
  D_Flip_Flop q3 (.clk(clock), .D(or_3_out), .Q(q3_out), .reset(q4_q));  // open: Qn, preset, en
  Hex_Digit_Display hex_digit_display_1 ();  // open: value, dp
  or or_4 (or_4_out, and_2_out, q1_q);
  or or_5 (or_5_out, and_3_out, q4_q);
  Hex_Digit_Display hex_digit_display_2 ();  // open: value, dp
  Hex_Digit_Display hex_digit_display_3 ();  // open: value, dp
  not not_4 (not_4_out, button);
  D_Flip_Flop q1 (.clk(clock), .D(or_4_out), .Q(q1_q), .reset(enable));  // open: Qn, preset, en
  D_Flip_Flop q4 (.clk(clock), .D(or_5_out), .Q(q4_q), .reset(reset));  // open: Qn, preset, en
  Hex_Digit_Display hex_digit_display_4 ();  // open: value, dp
  and and_4 (and_4_out, not_4_out, q1_q);
  or or_6 (or_6_out, and_4_out, enable);
  and and_5 (and_5_out, button, q4_q);
  or or_7 (or_7_out, and_5_out, reset);
  D_Flip_Flop q2 (.clk(clock), .D(or_6_out), .Q(enable), .reset(q3_out));  // open: Qn, preset, en
  not not_5 (not_5_out, button);
  D_Flip_Flop q5 (.clk(clock), .D(or_7_out), .Q(reset), .reset(q0_out));  // open: Qn, preset, en
  and and_6 (q2_out, button, enable);
  and and_7 (q5_out, not_5_out, reset);
endmodule

module test (
);

  wire and_1_out, and_2_out, and_3_out, and_4_out, and_5_out, and_6_out, Button, button_2_out, clock_1_out,
       IButton, or_1_out, or_2_out, or_3_out, Q1, Q2, Q3;

  Button button_1 (.out(Button));
  not not_1 (IButton, Button);
  and and_1 (and_1_out, Q1, IButton);
  and and_2 (and_2_out, Button, Q3);
  and and_3 (and_3_out, Q2, IButton);
  and and_4 (and_4_out, Button, Q1);
  and and_5 (and_5_out, Q3, IButton);
  and and_6 (and_6_out, Button, Q2);
  or or_1 (or_1_out, and_1_out, and_2_out);
  or or_2 (or_2_out, and_3_out, and_4_out);
  or or_3 (or_3_out, and_5_out, and_6_out);
  Clock clock_1 (.out(clock_1_out));
  D_Flip_Flop u_Q3 (.clk(clock_1_out), .D(or_3_out), .Q(Q3), .reset(button_2_out));  // open: Qn, preset, en
  D_Flip_Flop u_Q1 (.clk(clock_1_out), .D(or_1_out), .Q(Q1), .preset(button_2_out));  // open: Qn, en, reset
  D_Flip_Flop u_Q2 (.clk(clock_1_out), .D(or_2_out), .Q(Q2), .reset(button_2_out));  // open: Qn, preset, en
  Button button_2 (.out(button_2_out));
endmodule
