// Logisim project ford.circ as structural Verilog: 3 circuits, main circuit main
module main (
  input  warning
);

  wire and_1_out, and_2_out, and_3_out, and_4_out, and_5_out, and_6_out, clock_1_out, comodo_1_cmdd,
       comodo_1_cmdg, not_1_out, not_2_out, not_3_out, or_1_out, or_2_out, or_3_out;
  wire [1:0] joystick_1_x;
  wire [2:0] counter_1_q;

  Joystick #(.bits(2)) joystick_1 (.x(joystick_1_x));  // open: y
  // Probe on comodo_1_cmdg
  comodo comodo_1 (.I(joystick_1_x), .Warning(warning), .CmdG(comodo_1_cmdg), .CmdD(comodo_1_cmdd));
  // Probe on comodo_1_cmdd
  LED AVG (.in(or_1_out));
  or or_1 (or_1_out, counter_1_q[1], counter_1_q[0]);
  LED ARG3 (.in(and_1_out));
  and and_1 (and_1_out, counter_1_q[1], counter_1_q[0]);
  or or_2 (or_2_out, 1'b1, comodo_1_cmdd);
  LED ARG1 (.in(and_2_out));
  LED ARG2 (.in(and_3_out));
  and and_2 (and_2_out, not_1_out, counter_1_q[0]);
  and and_3 (and_3_out, counter_1_q[1], not_2_out);
  not not_1 (not_1_out, counter_1_q[1]);
  not not_2 (not_2_out, counter_1_q[0]);
  not not_3 (not_3_out, or_2_out);
  Counter #(.width(3), .max('h7)) counter_1 (
    .count(comodo_1_cmdg), .Q(counter_1_q), .clk(clock_1_out), .clr(not_3_out));  // open: load, D, carry
  Clock clock_1 (.out(clock_1_out));
  LED ARD2 (.in(and_5_out));
  LED ARD1 (.in(and_4_out));
  // AND_Gate and_4 has open pins: out=and_4_out
  // AND_Gate and_5 has open pins: out=and_5_out
  LED ARD3 (.in(and_6_out));
  // AND_Gate and_6 has open pins: out=and_6_out
  LED AVD (.in(or_3_out));
  // OR_Gate or_3 has open pins: out=or_3_out

  // Notes on the sheet:
  //   Gauche/Droite
endmodule

module comodo (
  input  Warning,
  input  [1:0] I,
  output CmdG,
  output CmdD
);

  wire and_1_out, and_2_out;

  and and_1 (and_1_out, I[0], ~I[1]);  // AND_Gate
  and and_2 (and_2_out, I[0], I[1]);
  or or_1 (CmdG, Warning, and_1_out);
  or or_2 (CmdD, Warning, and_2_out);
endmodule

module compteur (
  input  _2050Hz,
  output _1_5Hz
);

  wire not_1_out, not_2_out, not_3_out, not_4_out;
  wire [11:0] adder_1_out, multiplexer_1_out, register_1_q;

  Register #(.width(12)) register_1 (.D(multiplexer_1_out), .en(1'b1), .Q(register_1_q), .clk(_2050Hz));  // open: clr
  not not_1 (not_1_out, adder_1_out[3]);
  not not_2 (not_2_out, adder_1_out[5]);
  not not_3 (not_3_out, adder_1_out[7]);
  not not_4 (not_4_out, adder_1_out[9]);
  Multiplexer #(.width(12), .enable("false")) multiplexer_1 (
    .in0(adder_1_out), .in1({12{1'b0}}), .out(multiplexer_1_out), .sel(_1_5Hz));
  Adder #(.width(12)) adder_1 (.a(register_1_q), .b(12'h1), .out(adder_1_out), .cin(1'b0));  // open: cout
  and and_1 (_1_5Hz, adder_1_out[0], adder_1_out[1], adder_1_out[2], not_1_out, adder_1_out[4], not_2_out, adder_1_out[6], not_3_out, adder_1_out[8], not_4_out, adder_1_out[10]);
endmodule
