// Logisim project Alu.circ as structural Verilog: 1 circuit, main circuit ALU
module ALU (
  input  [7:0] arg1,
  input  [7:0] arg2,
  input  [3:0] codeOp,
  input  passtrough__invert,
  output [2:0] ZCN,
  output [7:0] out
);

  wire carryAdd, carrySub;
  wire [7:0] adder_1_out, and_1_out, or_1_out, subtractor_1_out, xor_1_out, xor_2_out;

  Adder adder_1 (.a(arg1), .b(arg2), .out(adder_1_out), .cin(1'b0), .cout(carryAdd));
  Subtractor subtractor_1 (.a(arg1), .b(arg2), .out(subtractor_1_out), .bin(1'b0), .bout(carrySub));
  assign and_1_out = arg1 & arg2;  // AND_Gate and_1, 8 bits wide
  assign or_1_out = arg1 | arg2;  // OR_Gate or_1, 8 bits wide
  assign xor_1_out = arg1 ^ arg2;  // XOR_Gate xor_1, 8 bits wide
  assign xor_2_out = arg1 ^ {8{passtrough__invert}};  // XOR_Gate xor_2, 8 bits wide
  Multiplexer #(.select(4), .width(8), .enable("false")) multiplexer_1 (
    .in0(adder_1_out), .in1(subtractor_1_out), .in2(and_1_out), .in3(or_1_out), .in4(xor_1_out),
    .in5({1'b0, arg1[7:1]}), .in6(subtractor_1_out), .in8(xor_2_out), .in9(arg2), .out(out), .sel(codeOp));  // open: in7, in10, in11, in12, in13, in14, in15
  nor nor_1 (ZCN[2], out[0], out[1], out[2], out[3], out[4], out[5], out[6], out[7]);
  Multiplexer #(.select(3), .disabled(0), .enable("false")) multiplexer_2 (
    .in0(carryAdd), .in1(carrySub), .in5(arg1[0]), .in6(carrySub), .out(ZCN[1]), .sel(codeOp[2:0]));  // open: in2, in3, in4, in7

  assign ZCN[0] = out[7];

  // Notes on the sheet:
  //   0000 add
  //   0001 sub
  //   0010 and
  //   0011 or
  //   0100 xor
  //   0110 cmp
  //   0101 lsr
  //   1000 passthrough/invert arg1
  //   1001 passthrough arg2
  //   (only meaningful for the "1000" operation. zero is"passtrough" / one is "invert")
endmodule
