// Logisim project MicroMachine.circ as structural Verilog: 5 circuits, main circuit Von Neumann machine
module Von_Neumann_machine (
  input  reset
);

  wire clock_out, cpu_1_m_we;
  wire [7:0] cpu_1_ma, cpu_1_mdo, ram_1_data;

  CPU cpu_1 (.MA(cpu_1_ma), .MDI(ram_1_data), .MDO(cpu_1_mdo), .M_we(cpu_1_m_we), .ck(clock_out), .reset(reset));
  Clock clock (.out(clock_out));
  // Probe on cpu_1_ma
  // Probe on cpu_1_mdo
  // Probe on ram_1_data
  RAM #(.bus("separate")) ram_1 (
    .addr(cpu_1_ma), .din(cpu_1_mdo), .data(ram_1_data), .str(cpu_1_m_we), .sel(1'b1), .clk(clock_out),
    .ld(1'b1));  // open: clr

  // Notes on the sheet:
  //   processor
  //   system bus
  //   address
  //   data: CPU to memory
  //   data: memory to CPU
  //   control: 1 means "write"
  //   memory
endmodule

module CPU (
  input  [7:0] MDI,
  input  ck,
  input  reset,
  output [7:0] MA,
  output [7:0] MDO,
  output M_we
);

  wire automate_1_cecst, automate_1_ceflags, automate_1_ceinstr, automate_1_cepc, automate_1_jr,
       automate_1_progfetch, automate_1_wedestreg;
  wire [2:0] data_path_1_flags;
  wire [7:0] data_path_1_ir;

  Automate automate_1 (
    .clock(ck), .enable(1'b1), .reset(reset), .progFetch(automate_1_progfetch), .ceInstr(automate_1_ceinstr),
    .ceFlags(automate_1_ceflags), .weDestReg(automate_1_wedestreg), .instruction(data_path_1_ir),
    .JR(automate_1_jr), .cePC(automate_1_cepc), .ceCST(automate_1_cecst));
  Data_Path data_path_1 (
    .weIR(automate_1_ceinstr), .doFetch(automate_1_progfetch), .memwrite(1'b0),
    .weDestReg(automate_1_wedestreg), .wePC(automate_1_cepc), .weCST(automate_1_cecst), .doJA(1'b0),
    .doJR(automate_1_jr), .weFlags(automate_1_ceflags), .IR(data_path_1_ir), .MA(MA), .MDI(MDI), .MDO(MDO),
    .M_we(M_we), .Flags(data_path_1_flags), .ck(ck), .reset(reset));

  // Notes on the sheet:
  //   FSM (Automate)
  //   Data Path
  //   Instruction
  //   Flags
  //   (memory address)
  //   (data in from mem)
  //   (data out to mem)
  //   (memory write enable)
endmodule

module Data_Path (
  input  weIR,
  input  doFetch,
  input  memwrite,
  input  weDestReg,
  input  wePC,
  input  weCST,
  input  doJA,
  input  doJR,
  input  weFlags,
  input  [7:0] MDI,
  input  ck,
  input  reset,
  output [7:0] IR,
  output [7:0] MA,
  output [7:0] MDO,
  output M_we,
  output [2:0] Flags
);

  wire comparator_1_eq, weA, weB;
  wire [2:0] alu_1_zcn;
  wire [7:0] adder_1_out, alu_1_out, multiplexer_2_out, multiplexer_3_out, multiplexer_4_out,
       multiplexer_5_out, regA, regB, regCST, regPC;

  // Probe on MDO
  Multiplexer #(.width(8), .enable("false")) multiplexer_1 (.in0(regA), .in1(regB), .out(MDO), .sel(IR[1]));
  // Probe on multiplexer_2_out
  Multiplexer #(.width(8), .enable("false")) multiplexer_2 (
    .in0(regA), .in1(regCST), .out(multiplexer_2_out), .sel(IR[2]));
  ALU alu_1 (
    .arg1(MDO), .arg2(multiplexer_2_out), .ZCN(alu_1_zcn), .out(alu_1_out), .codeOp(IR[6:3]),
    .passtrough__invert(IR[2]));
  Multiplexer #(.width(8), .enable("false")) multiplexer_3 (
    .in0(8'h1), .in1({{4{IR[4]}}, IR[3:0]}), .out(multiplexer_3_out), .sel(doJR));
  Adder adder_1 (.a(regPC), .b(multiplexer_3_out), .out(adder_1_out));  // open: cin, cout
  // Probe on Flags
  Register #(.width(3)) u_flags (.D(alu_1_zcn), .en(weFlags), .Q(Flags), .clk(ck), .clr(reset));
  // Probe on alu_1_out
  Multiplexer #(.width(8), .enable("false")) multiplexer_4 (
    .in0(alu_1_out), .in1(MDI), .out(multiplexer_4_out), .sel(comparator_1_eq));
  Comparator #(.width(4)) comparator_1 (.a(IR[6:3]), .b(4'b1101), .eq(comparator_1_eq));  // open: gt, lt
  Multiplexer #(.width(8), .enable("false")) multiplexer_5 (
    .in0(adder_1_out), .in1(regCST), .out(multiplexer_5_out), .sel(doJA));
  Register u_IR (.D(MDI), .en(weIR), .Q(IR), .clk(ck), .clr(reset));
  Register CST (.D(MDI), .en(weCST), .Q(regCST), .clk(ck), .clr(reset));
  // Probe on multiplexer_5_out
  Register PC (.D(multiplexer_5_out), .en(wePC), .Q(regPC), .clk(ck), .clr(reset));
  Register A (.D(multiplexer_4_out), .en(weA), .Q(regA), .clk(ck), .clr(reset));
  Register B (.D(multiplexer_4_out), .en(weB), .Q(regB), .clk(ck), .clr(reset));
  and and_1 (weA, ~IR[0], weDestReg);  // AND_Gate
  and and_2 (weB, IR[0], weDestReg);
  // Probe on multiplexer_2_out
  // Probe on MDI
  Multiplexer #(.width(8), .enable("false")) multiplexer_6 (
    .in0(multiplexer_2_out), .in1(regPC), .out(MA), .sel(doFetch));

  assign M_we = memwrite;

  // Other names for the same wires on the sheet: destS = IR[0]; offset[4:0] = IR[4:0]; arg1S = IR[1]; arg2S = IR[2];
  //   opcode[3:0] = IR[6:3]

  // Notes on the sheet:
  //   (Instruction)
  //   (memory address)
  //   (data out to mem)
  //   (memory write enable)
  //   (data in from mem)
endmodule

module ALU (
  input  [7:0] arg1,
  input  [7:0] arg2,
  input  [3:0] codeOp,
  input  passtrough__invert,
  output [2:0] ZCN,
  output [7:0] out
);

  wire carryAdd, carrySub;
  wire [7:0] adder_1_out, and_1_out, or_1_out, subtractor_1_out, xor_1_out, xor_2_out;

  Adder adder_1 (.a(arg1), .b(arg2), .out(adder_1_out), .cin(1'b0), .cout(carryAdd));
  Subtractor subtractor_1 (.a(arg1), .b(arg2), .out(subtractor_1_out), .bin(1'b0), .bout(carrySub));
  assign and_1_out = arg1 & arg2;  // AND_Gate and_1, 8 bits wide
  assign or_1_out = arg1 | arg2;  // OR_Gate or_1, 8 bits wide
  assign xor_1_out = arg1 ^ arg2;  // XOR_Gate xor_1, 8 bits wide
  assign xor_2_out = arg1 ^ {8{passtrough__invert}};  // XOR_Gate xor_2, 8 bits wide
  Multiplexer #(.select(4), .width(8), .enable("false")) multiplexer_1 (
    .in0(adder_1_out), .in1(subtractor_1_out), .in2(and_1_out), .in3(or_1_out), .in4(xor_1_out),
    .in5({1'b0, arg1[7:1]}), .in6(subtractor_1_out), .in8(xor_2_out), .in9(arg2), .out(out), .sel(codeOp));  // open: in7, in10, in11, in12, in13, in14, in15
  nor nor_1 (ZCN[2], out[0], out[1], out[2], out[3], out[4], out[5], out[6], out[7]);
  Multiplexer #(.select(3), .disabled(0), .enable("false")) multiplexer_2 (
    .in0(carryAdd), .in1(carrySub), .in5(arg1[0]), .in6(carrySub), .out(ZCN[1]), .sel(codeOp[2:0]));  // open: in2, in3, in4, in7

  assign ZCN[0] = out[7];

  // Notes on the sheet:
  //   0000 add
  //   0001 sub
  //   0010 and
  //   0011 or
  //   0100 xor
  //   0110 cmp
  //   0101 lsr
  //   1000 passthrough/invert arg1
  //   1001 passthrough arg2
  //   (only meaningful for the "1000" operation. zero is"passtrough" / one is "invert")
endmodule

module Automate (
  input  [7:0] instruction,
  input  enable,
  input  clock,
  input  reset,
  output cePC,
  output progFetch,
  output ceInstr,
  output weDestReg,
  output ceFlags,
  output JR,
  output ceCST
);

  wire and_1_out, and_2_out, and_3_out, IncrPC, InstrDecode, not_1_out, not_2_out, not_3_out, not_4_out,
       or_1_out, or_2_out;

  not not_1 (not_1_out, instruction[7]);
  not not_2 (not_2_out, instruction[7]);
  not not_3 (not_3_out, instruction[2]);
  not not_4 (not_4_out, instruction[2]);
  or or_1 (or_1_out, ceFlags, JR);
  and and_1 (and_1_out, not_1_out, not_3_out, InstrDecode);
  and and_2 (and_2_out, InstrDecode, not_4_out, instruction[7]);
  and and_3 (and_3_out, InstrDecode, not_2_out, instruction[2]);
  or or_2 (or_2_out, ceCST, and_1_out);
  D_Flip_Flop d_ff_1 (.clk(clock), .D(or_1_out), .Q(ceInstr), .preset(reset), .en(enable));  // open: Qn, reset
  D_Flip_Flop d_ff_2 (.clk(clock), .D(ceInstr), .Q(InstrDecode), .en(enable), .reset(reset));  // open: Qn, preset
  D_Flip_Flop d_ff_3 (.clk(clock), .D(or_2_out), .Q(ceFlags), .en(enable), .reset(reset));  // open: Qn, preset
  D_Flip_Flop d_ff_4 (.clk(clock), .D(and_2_out), .Q(JR), .en(enable), .reset(reset));  // open: Qn, preset
  D_Flip_Flop d_ff_5 (.clk(clock), .D(and_3_out), .Q(IncrPC), .en(enable), .reset(reset));  // open: Qn, preset
  D_Flip_Flop d_ff_6 (.clk(clock), .D(IncrPC), .Q(ceCST), .en(enable), .reset(reset));  // open: Qn, preset
  or or_3 (cePC, ceFlags, JR, IncrPC);
  or or_4 (progFetch, ceInstr, ceCST);

  assign weDestReg = ceFlags;

  // Other names for the same wires on the sheet: CstFetch = ceCST; DoJR = JR; InstrFetch = ceInstr;
  //   hasConst = instruction[2]; isJR = instruction[7]; RegWrite = ceFlags
endmodule
